# Fritzing sketch UltraSonic (saved by Fritzing 0.9.2b)
breadboards: 1

parts:
  U1 = LCD-16X2 [package=lcd-16x2_noholes]
  R1 = Rotary Potentiometer (Small) [maximum_resistance=100kΩ package=THT]
  SPKR1 = Loudspeaker
  パーツ1 = SRF05 Ultrasonic Rangefinder
  パーツ2 = Arduino Uno (Rev3)

nets:
  GND: U1.VSS, U1.R_W, U1.K, R1.leg2, SPKR1.pin1, パーツ1.GND, パーツ2.GND
  VDD: U1.VDD, U1.A, R1.leg1, パーツ1.VCC, パーツ2.5V
  N1: U1.VO, R1.wiper
  N2: U1.RS, パーツ2.D12/MISO
  N3: U1.E, パーツ2.D11_PWM/MOSI
  N4: U1.DB4, パーツ2.D5_PWM
  N5: U1.DB5, パーツ2.D4
  N6: U1.DB6, パーツ2.D3_PWM
  N7: U1.DB7, パーツ2.D2
  N8: SPKR1.pin2, パーツ2.D7
  N9: パーツ1.Trig, パーツ2.D8
  N10: パーツ1.Echo, パーツ2.D9_PWM

notes:
  1602A
  LCD
